// Digital circuit CMOS_Inverter.dig as structural Verilog
module CMOS_Inverter (
  input  in_2,
  output out_1
);

  wire pfet_1_s;

  PFET pfet_1 (.G(in_2), .S(pfet_1_s), .D(out_1));
  NFET nfet_1 (.G(in_2), .D(out_1), .S(1'b0));
endmodule
