// Digital circuit DigitalNumber.dig as structural Verilog
module DigitalNumber (
  input  i0,
  input  i1,
  input  i2,
  input  i3
);

  wire a, and_1_out, and_2_out, and_3_out, and_4_out, and_5_out, and_6_out, and_7_out, and_8_out, and_9_out,
       and_10_out, b, c, d, e, f, g, ip0, ip1, ip2, xnor_1_out, xnor_2_out, xor_1_out;

  Seven_Seg seven_seg_1 (.a(a), .b(b), .c(c), .d(d), .e(e), .f(f), .g(g), .dp(b));
  not not_1 (ip0, i0);
  not not_2 (ip1, i1);
  not not_3 (ip2, i2);
  xnor xnor_1 (xnor_1_out, i2, i0);
  xnor xnor_2 (xnor_2_out, i1, i0);
  and and_1 (and_1_out, i1, ip0);
  and and_2 (and_2_out, ip2, ip0);
  and and_3 (and_3_out, ip2, i1);
  and and_4 (and_4_out, i2, ip1, i0);
  and and_5 (and_5_out, i1, ip0);
  and and_6 (and_6_out, ip2, ip0);
  and and_7 (and_7_out, i2, ip1);
  and and_8 (and_8_out, i2, ip0);
  and and_9 (and_9_out, ip1, ip0);
  xor xor_1 (xor_1_out, i2, i1);
  and and_10 (and_10_out, i1, ip0);
  or or_1 (a, i3, i1, xnor_1_out);
  or or_2 (b, ip2, xnor_2_out);
  or or_3 (c, i2, ip1, i0);
  or or_4 (d, and_1_out, and_2_out, and_3_out, and_4_out);
  or or_5 (e, and_5_out, and_6_out);
  or or_6 (f, i3, and_7_out, and_8_out, and_9_out);
  or or_7 (g, i3, xor_1_out, and_10_out);
endmodule
