// Digital circuit Ej3Pag1.dig as structural Verilog
module Ej3Pag1 (
  input  x,
  input  y,
  input  z,
  output f
);

  wire nand_1_out, nand_2_out, nand_3_out, nand_4_out, nand_5_out, nand_6_out, nand_7_out, nand_8_out,
       nand_9_out, nand_10_out;

  nand nand_1 (nand_1_out, x, x, x);
  nand nand_2 (nand_2_out, y, y, y);
  nand nand_3 (nand_3_out, nand_1_out, z);
  nand nand_4 (nand_4_out, nand_1_out, z);
  nand nand_5 (nand_5_out, x, z);
  nand nand_6 (nand_6_out, x, y);
  nand nand_7 (nand_7_out, nand_3_out, nand_3_out, nand_4_out);
  nand nand_8 (nand_8_out, nand_5_out, nand_6_out, nand_6_out);
  nand nand_9 (nand_9_out, nand_7_out, nand_7_out, nand_7_out);
  nand nand_10 (nand_10_out, nand_8_out, nand_8_out, nand_8_out);
  nand nand_11 (f, nand_9_out, nand_10_out, nand_10_out);
endmodule
