// Digital circuit NAND3Entradas.dig as structural Verilog
module NAND3Entradas (
  input  A,
  input  C,
  input  _2,
  output \output 
);

  wire nfet_1_s, nfet_3_s, nfet_5_s, Output_1, Output_3;

  PFET pfet_1 (.G(A), .S(1'b1), .D(Output_3));
  NFET nfet_1 (.G(C), .D(Output_3), .S(nfet_1_s));
  NFET nfet_2 (.G(A), .D(nfet_1_s), .S(1'b0));
  PFET pfet_2 (.G(C), .S(1'b1), .D(Output_3));
  PFET pfet_3 (.G(Output_3), .S(1'b1), .D(Output_1));
  NFET nfet_3 (.G(Output_3), .D(Output_1), .S(nfet_3_s));
  NFET nfet_4 (.G(Output_3), .D(nfet_3_s), .S(1'b0));
  PFET pfet_4 (.G(Output_3), .S(1'b1), .D(Output_1));
  PFET pfet_5 (.G(Output_1), .S(1'b1), .D(\output ));
  NFET nfet_5 (.G(_2), .D(\output ), .S(nfet_5_s));
  NFET nfet_6 (.G(Output_1), .D(nfet_5_s), .S(1'b0));
  PFET pfet_6 (.G(_2), .S(1'b1), .D(\output ));

  // Other names for the same wires on the sheet: input_A = A; input_C = C; Output_2 = _2
endmodule
