// Digital circuit NAND_3Entradas_sencillo.dig as structural Verilog
module NAND_3Entradas_sencillo (
  input  in_2,
  input  in_3,
  input  in_4,
  output out_1
);

  wire nfet_1_s, nfet_2_s;

  FGPFET fgpfet_1 (.G(in_4), .S(1'b1), .D(out_1));
  FGPFET fgpfet_2 (.G(in_2), .S(1'b1), .D(out_1));
  FGPFET fgpfet_3 (.G(in_3), .S(1'b1), .D(out_1));
  NFET nfet_1 (.G(in_3), .D(out_1), .S(nfet_1_s));
  NFET nfet_2 (.G(in_2), .D(nfet_1_s), .S(nfet_2_s));
  NFET nfet_3 (.G(in_4), .D(nfet_2_s), .S(1'b0));

  // Other names for the same wires on the sheet: input_1 = in_4; input_2 = in_2; input_3 = in_3; input_A = out_1
endmodule
