// Digital circuit OR_con_NAND.dig as structural Verilog
module OR_con_NAND (
  input  A,
  input  B,
  output \output 
);

  wire nfet_1_s, nfet_3_s, nfet_5_s, Output_1, Output_2;

  PFET pfet_1 (.G(A), .S(1'b1), .D(Output_2));
  PFET pfet_2 (.G(B), .S(1'b1), .D(Output_1));
  NFET nfet_1 (.G(A), .D(Output_2), .S(nfet_1_s));
  NFET nfet_2 (.G(A), .D(nfet_1_s), .S(1'b0));
  NFET nfet_3 (.G(B), .D(Output_1), .S(nfet_3_s));
  NFET nfet_4 (.G(B), .D(nfet_3_s), .S(1'b0));
  PFET pfet_3 (.G(A), .S(1'b1), .D(Output_2));
  PFET pfet_4 (.G(B), .S(1'b1), .D(Output_1));
  PFET pfet_5 (.G(Output_2), .S(1'b1), .D(\output ));
  NFET nfet_5 (.G(Output_2), .D(\output ), .S(nfet_5_s));
  NFET nfet_6 (.G(Output_1), .D(nfet_5_s), .S(1'b0));
  PFET pfet_6 (.G(Output_1), .S(1'b1), .D(\output ));

  // Other names for the same wires on the sheet: input_A = A; input_B = B
endmodule
