// Digital circuit Counter_Register.dig as structural Verilog
module Counter_Register (
  input  En,
  input  Clock,
  input  C,
  input  Set,
  input  Counter,
  output out_5,
  output out_6,
  output out_7,
  output out_8,
  output Overflow
);

  wire and_2_out, and_3_out, and_4_out, multiplexer_1_out, multiplexer_2_out, multiplexer_3_out,
       multiplexer_4_out, xor_1_out, xor_2_out, xor_3_out, xor_4_out;

  Multiplexer multiplexer_1 (.sel(En), .in_0(out_5), .in_1(xor_1_out), .out(multiplexer_1_out));
  and and_1 (Overflow, out_5, and_2_out);
  xor xor_1 (xor_1_out, out_5, and_2_out);
  D_FF_AS d_ff_as_1 (.Set(Set), .D(multiplexer_1_out), .C(Clock), .Clr(C), .Q(out_5));  // open: nQ
  Multiplexer multiplexer_2 (.sel(En), .in_0(out_6), .in_1(xor_2_out), .out(multiplexer_2_out));
  and and_2 (and_2_out, out_6, and_3_out);
  xor xor_2 (xor_2_out, out_6, and_3_out);
  D_FF_AS d_ff_as_2 (.Set(Set), .D(multiplexer_2_out), .C(Clock), .Clr(C), .Q(out_6));  // open: nQ
  and and_3 (and_3_out, out_7, and_4_out);
  xor xor_3 (xor_3_out, out_7, and_4_out);
  Multiplexer multiplexer_3 (.sel(En), .in_0(out_7), .in_1(xor_3_out), .out(multiplexer_3_out));
  D_FF_AS d_ff_as_3 (.Set(Set), .D(multiplexer_3_out), .C(Clock), .Clr(C), .Q(out_7));  // open: nQ
  Multiplexer multiplexer_4 (.sel(En), .in_0(out_8), .in_1(xor_4_out), .out(multiplexer_4_out));
  and and_4 (and_4_out, out_8, Counter);
  xor xor_4 (xor_4_out, out_8, Counter);
  D_FF_AS d_ff_as_4 (.Set(Set), .D(multiplexer_4_out), .C(Clock), .Clr(C), .Q(out_8));  // open: nQ
endmodule
