// Digital circuit FlipFlop_SetClear_Plexer.dig as structural Verilog
module FlipFlop_SetClear_Plexer (
  input  D,
  input  Clear,
  input  Set,
  input  clk,
  input  En,
  output Q
);

  wire multiplexer_1_out, nand_1_out, nand_2_out, nand_3_out, nand_4_out, nand_5_out, nand_6_out, nand_8_out,
       not_1_out, not_2_out, not_3_out, not_4_out, not_5_out;

  Multiplexer multiplexer_1 (.sel(En), .in_0(Q), .in_1(D), .out(multiplexer_1_out));
  not not_1 (not_1_out, multiplexer_1_out);
  not not_2 (not_2_out, clk);
  not not_3 (not_3_out, Set);
  nand nand_1 (nand_1_out, multiplexer_1_out, not_2_out);
  nand nand_2 (nand_2_out, not_2_out, not_1_out);
  not not_4 (not_4_out, Clear);
  nand nand_3 (nand_3_out, not_3_out, nand_1_out, nand_4_out);
  nand nand_4 (nand_4_out, nand_3_out, nand_2_out, not_4_out);
  not not_5 (not_5_out, nand_3_out);
  nand nand_5 (nand_5_out, nand_3_out, clk);
  nand nand_6 (nand_6_out, clk, not_5_out);
  nand nand_7 (Q, not_3_out, nand_5_out, nand_8_out);
  nand nand_8 (nand_8_out, Q, nand_6_out, not_4_out);

  // Notes on the sheet:
  //   clk: Hz: 20
  //   Con el multiplexor puedo hacer un registro.
  //   Asi por medio del enable puedo decidir cuando cambiar el estado de Q al cambiar Data.
  //   Si esta desactivado el cambio de Data no produce cambio en Q.
endmodule
