// Digital circuit Register_1bit.dig as structural Verilog
module Register_1bit (
  input  D,
  input  En,
  input  Clock,
  input  C,
  input  S,
  output out_1
);

  wire multiplexer_1_out;

  Multiplexer multiplexer_1 (.sel(En), .in_0(out_1), .in_1(D), .out(multiplexer_1_out));
  D_FF_AS d_ff_as_1 (.Set(S), .D(multiplexer_1_out), .C(Clock), .Clr(C), .Q(out_1));  // open: nQ
endmodule
