// Digital circuit Demux_1Entrada.dig as structural Verilog
module Demux_1Entrada (
  input  D0,
  input  Sel1,
  input  Sel2,
  output S3,
  output S2,
  output S1,
  output S0
);

  wire not_1_out, not_2_out;

  not not_1 (not_1_out, Sel1);
  not not_2 (not_2_out, Sel2);
  and and_1 (S3, D0, Sel1, Sel2);
  and and_2 (S2, D0, Sel1, not_2_out);
  and and_3 (S1, D0, not_1_out, Sel2);
  and and_4 (S0, D0, not_1_out, not_2_out);

  // Notes on the sheet:
  //   Un demultiplexor redirige una entrada a varias salidas, solo una a la vez por medio del orden de activacion de los selectores.
  //   Al lado de cada salida se encuentra el estado de los selectores (Sel1, Sel2) para la seleccion de esa salida para el dato ingresado.
  //   (1,1)
  //   (1,0)
  //   (0,1)
  //   (0,0)
endmodule
