// Digital circuit FlipFlop_JK.dig as structural Verilog
module FlipFlop_JK (
  input  J,
  input  K,
  input  Clock,
  output Q,
  output Q_2
);

  wire and_1_out, and_2_out, nand_1_out, nand_2_out, nand_3_out, nand_4_out, nand_5_out, nand_6_out,
       nand_7_out;

  and and_1 (and_1_out, Q_2, J);
  and and_2 (and_2_out, Clock, K);
  nand nand_1 (nand_1_out, and_1_out, Clock);
  nand nand_2 (nand_2_out, and_2_out, Q);
  nand nand_3 (nand_3_out, nand_1_out, nand_4_out);
  nand nand_4 (nand_4_out, nand_3_out, nand_2_out);
  nand nand_5 (nand_5_out, Clock, Clock);
  nand nand_6 (nand_6_out, nand_3_out, nand_5_out);
  nand nand_7 (nand_7_out, nand_5_out, nand_4_out);
  nand nand_8 (Q, nand_6_out, Q_2);
  nand nand_9 (Q_2, Q, nand_7_out);

  // Notes on the sheet:
  //   Clock: Hz: 60
  //   Master
  //   El FlipFlop JK consta de dos Latch, denominados Master y Slave.
  //   Cuando las entradas J y K están apagadas, no se producira cambio alguno con el pulso del reloj, 
  //   es decir conservara el estado que tenia.
  //   Si se tiene la entrada J prendida y la K apagada la salida Q se activara con el pulso del reloj, y si se
  //   tiene el caso contrario, K prendido y J apagado, la salida Q estara apagada.
  //   Ahora bien, en el FlipFlop RS la opción de ambas entradas prendidas estaba prohibida, pero en este 
  //   FlipFlop este problema esta corregido.
  //   Por lo que al tener J y K prendidos con cada pulso del reloj Q cambiara de estado.
  //   Slave
endmodule
