// Digital circuit FlipFlop_RS.dig as structural Verilog
module FlipFlop_RS (
  input  S,
  input  R,
  input  Clock,
  output Q,
  output Q_2
);

  wire and_1_out, and_2_out, and_3_out, and_4_out, nand_1_out, nor_1_out, nor_2_out;

  and and_1 (and_1_out, S, Clock);
  and and_2 (and_2_out, Clock, R);
  nor nor_1 (nor_1_out, and_1_out, nor_2_out);
  nor nor_2 (nor_2_out, nor_1_out, and_2_out);
  nand nand_1 (nand_1_out, Clock, Clock);
  and and_3 (and_3_out, nor_1_out, nand_1_out);
  and and_4 (and_4_out, nand_1_out, nor_2_out);
  nor nor_3 (Q, and_3_out, Q_2);
  nor nor_4 (Q_2, Q, and_4_out);

  // Notes on the sheet:
  //   Clock: Hz: 60
  //   El FlipFlop RS consta de dos Latch, denominados Master y Slave.
  //   Existen dos estados fundamentales denominados Set y Reset. El estado Set se consigue cuando la entrada Set esta 
  //   prendida y la R apagada, lo que genera que en el pulso del reloj se active la salida Q. El estado Reset, por el contrario
  //   se produce cuando la entrada R esta prendida y la S esta apagada, esto hace que la salida Q se apague con el pulso
  //   del reloj. 
  //   Cuando las entradas S y R estan ambas apagadas con el pulso del reloj no se produce cambio en el estado de Q, 
  //   pero cuando ambas estan prendidas se produce un estado de oscilacion, por lo que es un estado prohibido.
  //   El FlipFlop JK corrige este estado por medio de una retroalimentacion.
  //   Master
  //   Slave
endmodule
