// Digital circuit Mux_8Entradas.dig as structural Verilog
module Mux_8Entradas (
  input  D7,
  input  D6,
  input  D5,
  input  D4,
  input  D3,
  input  D2,
  input  D1,
  input  D0,
  input  Sel1,
  input  Sel2,
  input  Sel3,
  output out_12
);

  wire and_1_out, and_2_out, and_3_out, and_4_out, and_5_out, and_6_out, and_7_out, and_8_out, not_1_out,
       not_2_out, not_3_out, or_1_out, or_2_out;

  not not_1 (not_1_out, Sel1);
  not not_2 (not_2_out, Sel2);
  not not_3 (not_3_out, Sel3);
  and and_1 (and_1_out, D7, Sel1, Sel2, Sel3);
  and and_2 (and_2_out, D6, Sel1, Sel2, not_3_out);
  and and_3 (and_3_out, D5, Sel1, not_2_out, Sel3);
  and and_4 (and_4_out, D4, not_1_out, Sel2, Sel3);
  and and_5 (and_5_out, D3, not_1_out, not_2_out, Sel3);
  and and_6 (and_6_out, D2, Sel1, not_2_out, not_3_out);
  and and_7 (and_7_out, D1, not_3_out, Sel2, not_1_out);
  and and_8 (and_8_out, D0, not_1_out, not_2_out, not_3_out);
  or or_1 (or_1_out, and_1_out, and_2_out, and_3_out, and_4_out);
  or or_2 (or_2_out, and_5_out, and_6_out, and_7_out, and_8_out);
  or or_3 (out_12, or_1_out, or_2_out);

  // Notes on the sheet:
  //   (1,1,1)
  //   (1,1,0)
  //   (1,0,1)
  //   (0,1,1)
  //   (0,0,1)
  //   (1,0,0)
  //   (0,1,0)
  //   (0,0,0)
  //   El multiplexor permite que de varias opciones, en este caso 8, seleccione solo una por medio del orden de activación de los selectores.
  //   Al lado de cada entrada está especificado el estado de los selectores (Sel1, Sel2, Sel3) para la selección de ese dato en específico.
endmodule
