// Digital circuit Registro_PinIO.dig as structural Verilog
module Registro_PinIO (
  input  D3,
  input  En,
  input  C,
  input  Set,
  input  D2,
  input  D1,
  input  D0,
  input  Ent3,
  input  En_2,
  input  C_2,
  input  Set_2,
  input  Ent2,
  input  Ent1,
  input  Ent0,
  input  En_3,
  input  C_3,
  input  Set_3,
  input  Clock,
  input  Clock_2,
  input  Clock_3,
  input  EntradaPinO0,
  input  EntradaPinO1,
  input  EntradaPinO2,
  input  EntradaPinO3,
  output Sal3,
  output Sal2,
  output Sal1,
  output Sal0,
  output SalidaPinI1,
  output SalidaPinI2,
  output SalidaPinI3,
  output SalidaPinI0
);

  wire D0_t, D0E, D0S, D1_t, D1E, D1S, D2_t, D2E, D2S, D3_t, D3E, D3S, multiplexer_1_out, multiplexer_2_out,
       multiplexer_3_out, multiplexer_4_out, multiplexer_5_out, multiplexer_6_out, multiplexer_7_out,
       multiplexer_8_out, multiplexer_9_out, multiplexer_10_out, multiplexer_11_out, multiplexer_12_out;

  Multiplexer multiplexer_1 (.sel(En), .in_0(D3_t), .in_1(D3), .out(multiplexer_1_out));
  D_FF_AS d_ff_as_1 (.Set(Set), .D(multiplexer_1_out), .C(Clock), .Clr(C), .Q(D3_t));  // open: nQ
  Multiplexer multiplexer_2 (.sel(En), .in_0(D2_t), .in_1(D2), .out(multiplexer_2_out));
  D_FF_AS d_ff_as_2 (.Set(Set), .D(multiplexer_2_out), .C(Clock), .Clr(C), .Q(D2_t));  // open: nQ
  Multiplexer multiplexer_3 (.sel(En), .in_0(D1_t), .in_1(D1), .out(multiplexer_3_out));
  D_FF_AS d_ff_as_3 (.Set(Set), .D(multiplexer_3_out), .C(Clock), .Clr(C), .Q(D1_t));  // open: nQ
  Multiplexer multiplexer_4 (.sel(En), .in_0(D0_t), .in_1(D0), .out(multiplexer_4_out));
  D_FF_AS d_ff_as_4 (.Set(Set), .D(multiplexer_4_out), .C(Clock), .Clr(C), .Q(D0_t));  // open: nQ
  Multiplexer multiplexer_5 (.sel(En_2), .in_0(D3E), .in_1(Ent3), .out(multiplexer_5_out));
  D_FF_AS d_ff_as_5 (.Set(Set_2), .D(multiplexer_5_out), .C(Clock_2), .Clr(C_2), .Q(D3E));  // open: nQ
  Multiplexer multiplexer_6 (.sel(En_2), .in_0(D2E), .in_1(Ent2), .out(multiplexer_6_out));
  D_FF_AS d_ff_as_6 (.Set(Set_2), .D(multiplexer_6_out), .C(Clock_2), .Clr(C_2), .Q(D2E));  // open: nQ
  assign SalidaPinI0 = D0_t ? D0E : 1'bz;  // Driver driver_1
  assign SalidaPinI1 = D1_t ? D1E : 1'bz;  // Driver driver_2
  assign SalidaPinI2 = D2_t ? D2E : 1'bz;  // Driver driver_3
  assign SalidaPinI3 = D3_t ? D3E : 1'bz;  // Driver driver_4
  Multiplexer multiplexer_7 (.sel(En_2), .in_0(D1E), .in_1(Ent1), .out(multiplexer_7_out));
  D_FF_AS d_ff_as_7 (.Set(Set_2), .D(multiplexer_7_out), .C(Clock_2), .Clr(C_2), .Q(D1E));  // open: nQ
  Multiplexer multiplexer_8 (.sel(En_2), .in_0(D0E), .in_1(Ent0), .out(multiplexer_8_out));
  D_FF_AS d_ff_as_8 (.Set(Set_2), .D(multiplexer_8_out), .C(Clock_2), .Clr(C_2), .Q(D0E));  // open: nQ
  Multiplexer multiplexer_9 (.sel(En_3), .in_0(Sal3), .in_1(D3S), .out(multiplexer_9_out));
  D_FF_AS d_ff_as_9 (.Set(Set_3), .D(multiplexer_9_out), .C(Clock_3), .Clr(C_3), .Q(Sal3));  // open: nQ
  Multiplexer multiplexer_10 (.sel(En_3), .in_0(Sal2), .in_1(D2S), .out(multiplexer_10_out));
  assign D0S = ~D0_t ? EntradaPinO0 : 1'bz;  // DriverInvSel driverinvsel_1
  assign D1S = ~D1_t ? EntradaPinO1 : 1'bz;  // DriverInvSel driverinvsel_2
  assign D2S = ~D2_t ? EntradaPinO2 : 1'bz;  // DriverInvSel driverinvsel_3
  assign D3S = ~D3_t ? EntradaPinO3 : 1'bz;  // DriverInvSel driverinvsel_4
  D_FF_AS d_ff_as_10 (.Set(Set_3), .D(multiplexer_10_out), .C(Clock_3), .Clr(C_3), .Q(Sal2));  // open: nQ
  Multiplexer multiplexer_11 (.sel(En_3), .in_0(Sal1), .in_1(D1S), .out(multiplexer_11_out));
  D_FF_AS d_ff_as_11 (.Set(Set_3), .D(multiplexer_11_out), .C(Clock_3), .Clr(C_3), .Q(Sal1));  // open: nQ
  Multiplexer multiplexer_12 (.sel(En_3), .in_0(Sal0), .in_1(D0S), .out(multiplexer_12_out));
  D_FF_AS d_ff_as_12 (.Set(Set_3), .D(multiplexer_12_out), .C(Clock_3), .Clr(C_3), .Q(Sal0));  // open: nQ

  // Notes on the sheet:
  //   Clock: Hz: 60
  //   Clock_2: Hz: 60
  //   Clock_3: Hz: 60
  //   Tres registros de 4 bits, de 4 Pines I/O.
  //   El primer registro es el registro de configuracion donde si esta prendido (1) se toma como un pin de entrada (I) 
  //   y si esta apagado (0) como un pin de salida (O).
  //   Este estado de entrada o salida llega a dos buffer tri-state donde de acuerdo al estado mutuamente excluyente 
  //   entre ellos, el Enable se activa o desactiva (para un estado de alta impedancia). 
  //   El segundo registro es un registro de almacenamiento para un pin de entrada, donde se almacena el estado que 
  //   proporciona Ent(0,1,2,3) del pin I en el output SalidaPinI(0,1,2,3).
  //   El tercer registro es un registro de control para un pin de salida, con el que se controla el estado del pin, este 
  //   control se realiza con EntradaPinO(0,1,2,3) y se ve reflejado en el output Sal(0,1,2,3).
  //   Registro de configuracion
  //   (Entrada/salida)
  //   Registro de almacenamiento
  //   (Entrada)
  //   Registro de control
  //   (Salida)
endmodule
